# Fritzing sketch SimGameController (saved by Fritzing 0.9.4)
breadboards: 5

parts:
  R1 = Slide Potentiometer [maximum_resistance=100kΩ]
  R2 = Slide Potentiometer [maximum_resistance=100kΩ]
  R3 = Slide Potentiometer [maximum_resistance=100kΩ]
  Composant1 = Arduino Due (Rev2b)
  Composant2 = Thumb Joystick
  Composant3 = Thumb Joystick
  Composant4 = Thumb Joystick  # not connected
  Composant5 = LCD1602-I2C  # not connected
  S1 = Round Pushbutton  # not connected
  S2 = Round Pushbutton  # not connected
  S3 = Round Pushbutton  # not connected
  S4 = Round Pushbutton  # not connected
  S5 = Round Pushbutton  # not connected
  S6 = Round Pushbutton  # not connected
  S7 = Round Pushbutton  # not connected
  S8 = Round Pushbutton  # not connected
  X1 = USB Connectors [package=usb-microb]  # not connected
  Toggle_2 = Taiway 100-SP-X-T1 SPDT Miniature Toggle Switch [part_number=100-SP-X-T1-0-0-B1-M1 package=THT]
  Toggle_3 = Taiway 100-SP-X-T1 SPDT Miniature Toggle Switch [part_number=100-SP-X-T1-0-0-B1-M1 package=THT]
  Toggle_4 = Taiway 100-SP-X-T1 SPDT Miniature Toggle Switch [part_number=100-SP-X-T1-0-0-B1-M1 package=THT]
  Toggle_1 = Taiway 100-SP-X-T1 SPDT Miniature Toggle Switch [part_number=100-SP-X-T1-0-0-B1-M1 package=THT]
  Button_2 = Round Pushbutton
  Button_1 = Round Pushbutton
  sideAxe1 = Rotary Encoder [package=THT]
  sideAxe2 = Rotary Encoder [package=THT]
  Button_3 = Round Pushbutton
  J3 = Camdenboss CTB0158-10 [part_number=CTB0158-10 package=THT]
  J4 = Camdenboss CTB0158-11 [part_number=CTB0158-11 package=THT]
  R4 = Resistor [tolerance=±5% resistance=10k package=THT]
  R5 = Resistor [tolerance=±5% resistance=10k package=THT]
  R6 = Resistor [tolerance=±5% resistance=10k package=THT]
  R7 = Resistor [tolerance=±5% resistance=10k package=THT]
  R8 = Resistor [tolerance=±5% resistance=10k package=THT]
  R9 = Resistor [tolerance=±5% resistance=10k package=THT]
  R10 = Resistor [tolerance=±5% resistance=10k package=THT]
  R11 = Resistor [tolerance=±5% resistance=10k package=THT]
  R12 = Resistor [tolerance=±5% resistance=10k package=THT]
  R13 = Resistor [tolerance=±5% resistance=10k package=THT]
  R14 = Resistor [tolerance=±5% resistance=10k package=THT]
  R15 = Resistor [tolerance=±5% resistance=10k package=THT]
  R16 = Resistor [tolerance=±5% resistance=10k package=THT]
  R17 = Resistor [tolerance=±5% resistance=10k package=THT]
  R18 = Resistor [tolerance=±5% resistance=10k package=THT]
  R19 = Resistor [tolerance=±5% resistance=10k package=THT]
  R20 = Resistor [tolerance=±5% resistance=10k package=THT]
  R21 = Resistor [tolerance=±5% resistance=10k package=THT]
  R22 = Resistor [tolerance=±5% resistance=10k package=THT]
  R23 = Resistor [tolerance=±5% resistance=10k package=THT]
  R24 = Resistor [tolerance=±5% resistance=10k package=THT]
  R25 = Resistor [tolerance=±5% resistance=10k package=THT]
  R26 = Resistor [tolerance=±5% resistance=10k package=THT]
  R27 = Resistor [tolerance=±5% resistance=10k package=THT]
  Button_4 = Round Pushbutton
  Button_5 = Round Pushbutton  # not connected
  Button_6 = Round Pushbutton  # not connected
  J5 = Camdenboss CTB0158-11 [part_number=CTB0158-11 package=THT]
  GRAPH_1 = LED_BARGRAPH_10 [package=led_bargaph_10]
  GRAPH_2 = LED_BARGRAPH_10 [package=led_bargaph_10]  # not connected
  buttonUp = Round Pushbutton
  buttonLeft = Round Pushbutton
  buttonRight = Round Pushbutton
  buttonDown = Round Pushbutton
  buttonSelect = Round Pushbutton
  S9 = Round Pushbutton
  J6 = Camdenboss CTB0158-11 [part_number=CTB0158-11 package=THT]
  U1 = 74HC595 [package="DIP16 [THT]"]
  U2 = 74HC595 [package="DIP16 [THT]"]
  GRAPH_3 = LED_BARGRAPH_10 [package=led_bargaph_10]
  U3 = 74HC595 [package="DIP16 [THT]"]

nets:
  VCC: R1.leg1, R2.leg1, R3.leg1, Composant2.VCC, Composant3.VCC, J3.pin2
  N1: R1.wiper, J4.pin7
  GND: R1.leg2, R2.leg2, R3.leg2, Composant2.GND, Composant3.GND, Toggle_2.COM, Toggle_3.COM, Toggle_4.COM, Toggle_1.COM, Button_2.leg1, Button_1.leg1, sideAxe1.EncoderPinC, sideAxe1.SwitchPinE, sideAxe2.EncoderPinC, sideAxe2.SwitchPinE, Button_3.leg0, J3.pin1, Button_4.leg0
  N2: R2.wiper, J4.pin6
  N3: R3.wiper, J4.pin5
  N4: Composant1.IOREF, R4.Pin_0, R5.Pin_0, R6.Pin_0, R7.Pin_0, R8.Pin_0, R9.Pin_0, R10.Pin_0, R11.Pin_0, R12.Pin_0, R13.Pin_0, R14.Pin_0, R15.Pin_0, R16.Pin_0, R17.Pin_0, R18.Pin_0, R19.Pin_0, R20.Pin_0, R21.Pin_0, R22.Pin_0, R23.Pin_0, R24.Pin_0, R25.Pin_0, R26.Pin_0, R27.Pin_0
  N5: Composant1.D38, R13.Pin_1
  N6: Composant1.D39, R12.Pin_1
  N7: Composant1.D40, R15.Pin_1
  N8: Composant1.D41, R14.Pin_1
  N9: Composant1.D42, R17.Pin_1
  N10: Composant1.D43, R16.Pin_1
  N11: Composant1.D44, R19.Pin_1
  N12: Composant1.D45, R18.Pin_1
  N13: Composant1.D46, R21.Pin_1
  N14: Composant1.D47, R20.Pin_1
  N15: Composant1.D48, R23.Pin_1
  N16: Composant1.D49, R22.Pin_1
  N17: Composant1.D50, R25.Pin_1
  N18: Composant1.D51, R24.Pin_1
  N19: Composant1.D52, R27.Pin_1
  N20: Composant1.D53, R26.Pin_1
  N21: Composant2.SEL, J3.pin5
  N22: Composant2.HORZ, J3.pin4
  N23: Composant2.VERT, J3.pin3
  N24: Composant3.SEL, J3.pin6
  N25: Composant3.HORZ, J3.pin7
  N26: Composant3.VERT, J3.pin8
  N27: Toggle_2.L1, J4.pin1
  N28: Toggle_2.L2, J4.pin8
  N29: Toggle_3.L1, J3.pin10
  N30: Toggle_3.L2, J4.pin9
  N31: Toggle_4.L1, J3.pin9
  N32: Toggle_4.L2, J4.pin10
  N33: Toggle_1.L1, J4.pin2
  N34: Toggle_1.L2, J4.pin11
  N35: Button_2.leg0, J4.pin3
  N36: Button_1.leg0, J4.pin4
  N37: sideAxe1.SwitchrPinD, J5.pin1
  N38: sideAxe2.SwitchrPinD, J5.pin2
  N39: Button_3.leg1, J5.pin3
  N40: Button_4.leg1, J5.pin4
  N41: GRAPH_1.A_A, U2.Q0
  N42: GRAPH_1.B_A, U2.Q1
  N43: GRAPH_1.C_A, U2.Q2
  N44: GRAPH_1.D_A, U2.Q3
  N45: GRAPH_1.E_A, U2.Q4
  N46: GRAPH_1.F_A, U2.Q5
  N47: GRAPH_1.G_A, U2.Q6
  N48: GRAPH_1.H_A, U2.Q7
  N49: GRAPH_1.I_A, U1.Q0
  N50: GRAPH_1.J_A, U1.Q1
  N51: GRAPH_1.J_C, GRAPH_1.I_C, GRAPH_1.H_C, GRAPH_1.G_C, GRAPH_1.F_C, GRAPH_1.E_C, GRAPH_1.D_C, GRAPH_1.C_C, GRAPH_1.B_C, GRAPH_1.A_C
  N52: buttonUp.leg0, buttonLeft.leg0, buttonRight.leg0, buttonDown.leg0, buttonSelect.leg0, S9.leg0, J6.pin1
  N53: buttonUp.leg1, J6.pin2
  N54: buttonLeft.leg1, J6.pin4
  N55: buttonRight.leg1, J6.pin5
  N56: buttonDown.leg1, J6.pin3
  N57: buttonSelect.leg1, J6.pin6
  N58: S9.leg1, J6.pin7
  N59: U1.Q2, GRAPH_3.A_A
  N60: U1.Q3, GRAPH_3.B_A
  N61: U1.Q4, GRAPH_3.C_A
  N62: U1.Q5, GRAPH_3.D_A
  N63: U1.Q6, GRAPH_3.E_A
  N64: U1.Q7, GRAPH_3.F_A
  GND_2: U1.GND, U2.GND
  N65: GRAPH_3.G_A, U3.Q0
  N66: GRAPH_3.H_A, U3.Q1
  N67: GRAPH_3.I_A, U3.Q2
  N68: GRAPH_3.J_A, U3.Q3
  N69: GRAPH_3.J_C, GRAPH_3.I_C, GRAPH_3.H_C, GRAPH_3.G_C, GRAPH_3.F_C, GRAPH_3.E_C, GRAPH_3.D_C, GRAPH_3.C_C, GRAPH_3.B_C, GRAPH_3.A_C

notes:
  Ne pas oublier 3.3V
  RIGHT SIDE
  FRONT PANNEL
  3.3 VOLT !
  Button input
  VCC
  GND
  Vertical Left
  Honrizontal Left
  BUTTON LEFT
  BUTTON RIGHT
  Honrizontal Right
  Vertical Right
  Slider 1 OUT
  Slider 2 OUT
  Slider 3 OUT
  Switch
  1    2    3    4    5    6
  7    8    9   10
  Toggle 2 Down
  Toggle 3 Down
  Toggle 4 Down
  Toggle 1 Down
  Toggle 4 UP
  Toggle 3 UP
  Toggle 2 UP
  Toggle 1 UP
  Button 2
  Button 1
  BUTTON 3
  BUTTON 4
  BUTTON 5
  BUTTON 6

custom parts:
  LCD1602-I2C: A standard character display, usually with 2x16 characters. Comes in many colors with LCM1602 IIC attached.
  Rotary Encoder: Rotary Encoder from ALPSec11e with switch.
